# Fritzing sketch RobotBuggy (saved by Fritzing 0.9.3b)
breadboards: 1

parts:
  Raspberry_Pi_1 = Raspberry Pi B+
  R1 = Resistor [tolerance=±5% resistance=330 package=THT]
  R2 = Resistor [tolerance=±5% resistance=680 package=THT]
  hc-sr2 = hc-sr04

nets:
  N1: Raspberry_Pi_1.GPIO4, hc-sr2.Trig
  GND: Raspberry_Pi_1.GND, hc-sr2.GND
  N2: Raspberry_Pi_1.GPIO17, R2.Pin_0
  5V: Raspberry_Pi_1.5V, hc-sr2.VCC
  N3: R1.Pin_0, R2.Pin_1
  N4: R1.Pin_1, hc-sr2.Echo
